// Logisim project Logisim_Schematic.circ as structural Verilog: 1 circuit, main circuit main
module main (
);

  wire and_1_out, buffer_1_out, button_1_out, button_2_out, button_3_out, clock_1_out, clock_2_out, d_ff_1_q,
       decoder_1_out0, decoder_1_out1, decoder_1_out2, decoder_1_out3, nand_1_out, nand_2_out, nand_3_out,
       nand_4_out, nand_5_out, nand_6_out, not_1_out, not_2_out, or_1_out, or_2_out, pull_resistor_2_node,
       switch_3_p2;
  wire [1:0] controlled_buffer_1_out;
  wire [2:0] d_ff_2_q;
  wire [3:0] counter_1_q, counter_2_q, register_6_q;
  wire [3:1] nor_1_out;
  wire [5:0] controlled_buffer_1_out_2;
  wire [6:6] or_3_out;
  wire [7:0] adder_1_out, and_2_out, and_3_out, and_4_out, and_5_out, and_6_out, bit_extender_1_out,
       bit_extender_2_out, bit_extender_3_out, bit_extender_4_out, controlled_buffer_6_out, counter_3_q,
       dipswitch_1_sw8, multiplexer_1_out, multiplexer_2_out, not_3_out, or_4_out, pull_resistor_5_node,
       ram_1_dout, register_1_q, register_2_q, register_3_q, register_4_q, register_5_q, rom_1_data,
       rom_2_data, rom_3_data, rom_4_data, rom_5_data, shifter_1_out, shifter_2_out, undriven, xor_1_out,
       xor_2_out;
  wire [10:10] pull_resistor_1_node;

  Counter #(.max('hf), .width(4)) counter_1 (
    .clr(counter_1_q[2]), .load(1'b0), .up(1'b1), .count(1'b1), .clk(clock_1_out), .D(4'b0000),
    .Q(counter_1_q));  // open: carry
  Clock clock_1 (.out(clock_1_out));
  Pull_Resistor pull_resistor_1 (.node(pull_resistor_1_node[10]));
  // Switch switch_1: pin names not known; wires that end beside it: 1'b1, pull_resistor_1_node[10]
  Register register_1 (
    .D({controlled_buffer_1_out, controlled_buffer_1_out_2}), .en(rom_5_data[3]), .clk(nand_5_out),
    .Q(register_1_q), .clr(or_3_out[6]));
  DipSwitch dipswitch_1 (
    .sw1(dipswitch_1_sw8[7]), .sw2(dipswitch_1_sw8[6]), .sw3(dipswitch_1_sw8[5]), .sw4(dipswitch_1_sw8[4]),
    .sw5(dipswitch_1_sw8[3]), .sw6(dipswitch_1_sw8[2]), .sw7(dipswitch_1_sw8[1]), .sw8(dipswitch_1_sw8[0]));
  Pull_Resistor pull_resistor_2 (.node(pull_resistor_2_node));
  // Switch switch_2: pin names not known; wires that end beside it: 1'b1, pull_resistor_2_node
  Button button_1 (.out(button_1_out));
  or or_1 (or_1_out, button_1_out, and_1_out);
  not not_1 (not_1_out, pull_resistor_2_node);
  and and_1 (and_1_out, nand_5_out, rom_2_data[1]);
  // DipSwitch dipswitch_2: pin names not known
  ROM #(.addrWidth(12)) rom_1 (
    .addr({1'b0, pull_resistor_1_node[10], counter_1_q[1:0], register_1_q}), .data(rom_1_data));
  or or_2 (or_2_out, or_3_out[6], d_ff_1_q);
  Counter #(.max('hf), .width(4)) counter_2 (
    .clr(or_2_out), .load(1'b0), .up(1'b1), .count(1'b1), .clk(nand_4_out), .D(4'b0000), .Q(counter_2_q));  // open: carry
  Button button_2 (.out(button_2_out));
  // Switch switch_3: pin names not known; wires that end beside it: 1'b1, switch_3_p2
  Pull_Resistor pull_resistor_3 (.node(switch_3_p2));
  Clock clock_2 (.out(clock_2_out));
  Multiplexer #(.width(8)) multiplexer_1 (
    .in0(dipswitch_1_sw8), .in1(register_2_q), .out(multiplexer_1_out), .sel(not_1_out));
  LedBar ledbar_1 (
    .led0(multiplexer_1_out[7]), .led1(multiplexer_1_out[6]), .led2(multiplexer_1_out[5]),
    .led3(multiplexer_1_out[4]), .led4(multiplexer_1_out[3]), .led5(multiplexer_1_out[2]),
    .led6(multiplexer_1_out[1]), .led7(multiplexer_1_out[0]));
  RAM #(.addrWidth(12), .trigger("high"), .\type ("nonvolatile")) ram_1 (
    .addr({4'b0000, multiplexer_1_out}), .we(or_1_out), .oe(1'b1), .din(multiplexer_2_out), .dout(ram_1_dout));
  Multiplexer #(.width(8)) multiplexer_2 (
    .in0(undriven), .in1({controlled_buffer_1_out, controlled_buffer_1_out_2}), .out(multiplexer_2_out),
    .sel(not_1_out));
  D_Flip_Flop d_ff_1 (.clk(nand_4_out), .Q(d_ff_1_q), .preset(rom_2_data[5]), .reset(nand_4_out));  // open: D, Qn
  not not_2 (not_2_out, switch_3_p2);
  LedBar #(.matrixcols(3)) ledbar_2 (.led0(d_ff_2_q[2]), .led1(d_ff_2_q[1]), .led2(d_ff_2_q[0]));
  nand nand_1 (nand_1_out, button_2_out, not_2_out);
  nand nand_2 (nand_2_out, switch_3_p2, clock_2_out);
  Register register_2 (
    .D({controlled_buffer_1_out, controlled_buffer_1_out_2}), .en(rom_3_data[7]), .clk(nand_5_out),
    .Q(register_2_q), .clr(or_3_out[6]));
  Decoder #(.enable("false"), .select(2)) decoder_1 (
    .out0(decoder_1_out0), .out1(decoder_1_out1), .out2(decoder_1_out2), .out3(decoder_1_out3),
    .sel(counter_1_q[1:0]));
  LedBar #(.matrixcols(6)) ledbar_3 (
    .led0(register_3_q[5]), .led1(register_3_q[4]), .led2(register_3_q[3]), .led3(register_3_q[2]),
    .led4(register_3_q[1]), .led5(register_3_q[0]));
  ROM #(.addrWidth(12)) rom_2 (.addr({d_ff_2_q, register_3_q[5:0], counter_2_q[2:0]}), .data(rom_2_data));
  ROM #(.addrWidth(12)) rom_3 (.addr({d_ff_2_q, register_3_q[5:0], counter_2_q[2:0]}), .data(rom_3_data));
  ROM #(.addrWidth(12)) rom_4 (.addr({d_ff_2_q, register_3_q[5:0], counter_2_q[2:0]}), .data(rom_4_data));
  ROM #(.addrWidth(12)) rom_5 (.addr({d_ff_2_q, register_3_q[5:0], counter_2_q[2:0]}), .data(rom_5_data));
  nand nand_3 (nand_3_out, nand_1_out, nand_2_out);
  nand nand_4 (nand_4_out, nand_3_out, nand_6_out);
  assign bit_extender_1_out = {{7{decoder_1_out0}}, decoder_1_out0};  // Bit_Extender bit_extender_1
  assign bit_extender_2_out = {{7{decoder_1_out1}}, decoder_1_out1};  // Bit_Extender bit_extender_2
  assign bit_extender_3_out = {{7{decoder_1_out2}}, decoder_1_out2};  // Bit_Extender bit_extender_3
  assign bit_extender_4_out = {{7{decoder_1_out3}}, decoder_1_out3};  // Bit_Extender bit_extender_4
  Register register_3 (
    .D({controlled_buffer_1_out, controlled_buffer_1_out_2}), .en(rom_2_data[4]), .clk(nand_5_out),
    .Q(register_3_q), .clr(or_3_out[6]));
  LedBar #(.matrixcols(3)) ledbar_4 (.led0(counter_2_q[2]), .led1(counter_2_q[1]), .led2(counter_2_q[0]));
  nand nand_5 (nand_5_out, nand_4_out, nand_4_out);
  nand nand_6 (nand_6_out, rom_2_data[7], rom_2_data[7]);
  assign {controlled_buffer_1_out, controlled_buffer_1_out_2} = rom_2_data[0] ? ram_1_dout : 8'bz;  // Controlled_Buffer controlled_buffer_1
  assign and_2_out = rom_1_data & bit_extender_1_out;  // AND_Gate and_2, 8 bits wide
  _7_Segment_Display u_7_segment_display_1 (
    .g(and_5_out[1]), .f(and_5_out[2]), .a(and_5_out[7]), .b(and_5_out[6]), .e(and_5_out[3]),
    .d(and_5_out[4]), .c(and_5_out[5]), .dp(and_5_out[0]));
  assign and_3_out = rom_1_data & bit_extender_2_out;  // AND_Gate and_3, 8 bits wide
  assign and_4_out = rom_1_data & bit_extender_3_out;  // AND_Gate and_4, 8 bits wide
  assign and_5_out = rom_1_data & bit_extender_4_out;  // AND_Gate and_5, 8 bits wide
  _7_Segment_Display u_7_segment_display_2 (
    .g(and_4_out[1]), .f(and_4_out[2]), .a(and_4_out[7]), .b(and_4_out[6]), .e(and_4_out[3]),
    .d(and_4_out[4]), .c(and_4_out[5]), .dp(and_4_out[0]));
  _7_Segment_Display u_7_segment_display_3 (
    .g(and_3_out[1]), .f(and_3_out[2]), .a(and_3_out[7]), .b(and_3_out[6]), .e(and_3_out[3]),
    .d(and_3_out[4]), .c(and_3_out[5]), .dp(and_3_out[0]));
  LedBar ledbar_5 (
    .led0(register_3_q[7]), .led1(register_3_q[6]), .led2(register_3_q[5]), .led3(register_3_q[4]),
    .led4(register_3_q[3]), .led5(register_3_q[2]), .led6(register_3_q[1]), .led7(register_3_q[0]));
  LedBar ledbar_6 (
    .led0(controlled_buffer_1_out[1]), .led1(controlled_buffer_1_out[0]),
    .led2(controlled_buffer_1_out_2[5]), .led3(controlled_buffer_1_out_2[4]),
    .led4(controlled_buffer_1_out_2[3]), .led5(controlled_buffer_1_out_2[2]),
    .led6(controlled_buffer_1_out_2[1]), .led7(controlled_buffer_1_out_2[0]));
  _7_Segment_Display u_7_segment_display_4 (
    .g(and_2_out[1]), .f(and_2_out[2]), .a(and_2_out[7]), .b(and_2_out[6]), .e(and_2_out[3]),
    .d(and_2_out[4]), .c(and_2_out[5]), .dp(and_2_out[0]));
  Button button_3 (.out(button_3_out));
  LedBar ledbar_7 (
    .led0(controlled_buffer_1_out[1]), .led1(controlled_buffer_1_out[0]),
    .led2(controlled_buffer_1_out_2[5]), .led3(controlled_buffer_1_out_2[4]),
    .led4(controlled_buffer_1_out_2[3]), .led5(controlled_buffer_1_out_2[2]),
    .led6(controlled_buffer_1_out_2[1]), .led7(controlled_buffer_1_out_2[0]));
  Pull_Resistor pull_resistor_4 (.node({controlled_buffer_1_out, controlled_buffer_1_out_2}));
  or or_3 (or_3_out[6], button_3_out, rom_2_data[6]);
  assign controlled_buffer_1_out[1] = rom_2_data[2] ? rom_2_data[2] : 1'bz;  // Controlled_Buffer controlled_buffer_2
  assign controlled_buffer_1_out_2[0] = rom_2_data[3] ? rom_2_data[3] : 1'bz;  // Controlled_Buffer controlled_buffer_3
  // LedBar #(.inputtype("row")) ledbar_8: pin names not known; wires that end beside it: rom_2_data
  // LedBar #(.inputtype("row")) ledbar_9: pin names not known; wires that end beside it: rom_3_data
  // LedBar #(.inputtype("row")) ledbar_10: pin names not known; wires that end beside it: rom_4_data
  // LedBar #(.inputtype("row")) ledbar_11: pin names not known; wires that end beside it: rom_5_data
  Counter counter_3 (
    .clr(or_3_out[6]), .load(rom_3_data[5]), .up(1'b1), .count(buffer_1_out), .clk(nand_5_out),
    .D({1'b0, or_3_out[6], controlled_buffer_1_out_2}), .Q(counter_3_q));  // open: carry
  buf buffer_1 (buffer_1_out, rom_3_data[4]);
  assign {controlled_buffer_1_out, controlled_buffer_1_out_2} = rom_3_data[3] ? register_4_q : 8'bz;  // Controlled_Buffer controlled_buffer_4
  Register register_4 (
    .D({controlled_buffer_1_out, controlled_buffer_1_out_2}), .en(rom_3_data[2]), .clk(nand_5_out),
    .Q(register_4_q), .clr(or_3_out[6]));
  assign {controlled_buffer_1_out, controlled_buffer_1_out_2} = rom_3_data[1] ? register_5_q : 8'bz;  // Controlled_Buffer controlled_buffer_5
  Register register_5 (
    .D({controlled_buffer_1_out, controlled_buffer_1_out_2}), .en(rom_3_data[0]), .clk(nand_5_out),
    .Q(register_5_q), .clr(or_3_out[6]));
  LedBar ledbar_12 (
    .led0(register_4_q[7]), .led1(register_4_q[6]), .led2(register_4_q[5]), .led3(register_4_q[4]),
    .led4(register_4_q[3]), .led5(register_4_q[2]), .led6(register_4_q[1]), .led7(register_4_q[0]));
  LedBar ledbar_13 (
    .led0(register_5_q[7]), .led1(register_5_q[6]), .led2(register_5_q[5]), .led3(register_5_q[4]),
    .led4(register_5_q[3]), .led5(register_5_q[2]), .led6(register_5_q[1]), .led7(register_5_q[0]));
  ROM rom_6 (.addr(controlled_buffer_6_out), .data({controlled_buffer_1_out, controlled_buffer_1_out_2}));
  assign controlled_buffer_6_out = rom_3_data[6] ? counter_3_q : 8'bz;  // Controlled_Buffer controlled_buffer_6
  Pull_Resistor pull_resistor_5 (.node(pull_resistor_5_node));
  assign pull_resistor_5_node = rom_4_data[7] ? {8{1'b1}} : 8'bz;  // Controlled_Buffer controlled_buffer_7
  Adder adder_1 (.a(register_4_q), .b(xor_1_out), .out(adder_1_out), .cin(rom_4_data[7]), .cout(nor_1_out[2]));
  assign xor_1_out = pull_resistor_5_node ^ register_5_q;  // XOR_Gate xor_1, 8 bits wide
  Comparator comparator_1 (.a(register_4_q), .b(register_5_q), .gt(nor_1_out[3]));  // open: eq, lt
  assign and_6_out = register_4_q & register_5_q;  // AND_Gate and_6, 8 bits wide
  assign or_4_out = register_4_q | register_5_q;  // OR_Gate or_4, 8 bits wide
  assign xor_2_out = register_4_q ^ register_5_q;  // XOR_Gate xor_2, 8 bits wide
  assign not_3_out = ~register_4_q;  // NOT_Gate not_3, 8 bits wide
  Shifter #(.shift("ar")) shifter_1 (.in(register_4_q), .\dist (3'b001), .out(shifter_1_out));
  Shifter shifter_2 (.in(register_4_q), .\dist (3'b001), .out(shifter_2_out));
  assign {controlled_buffer_1_out, controlled_buffer_1_out_2} = rom_4_data[6] ? adder_1_out : 8'bz;  // Controlled_Buffer controlled_buffer_8
  Pull_Resistor pull_resistor_6 (.node(nor_1_out[2]));
  assign {controlled_buffer_1_out, controlled_buffer_1_out_2} = rom_4_data[5] ? and_6_out : 8'bz;  // Controlled_Buffer controlled_buffer_9
  assign {controlled_buffer_1_out, controlled_buffer_1_out_2} = rom_4_data[4] ? or_4_out : 8'bz;  // Controlled_Buffer controlled_buffer_10
  nor nor_1 (nor_1_out[1], adder_1_out[0], adder_1_out[1], adder_1_out[2], adder_1_out[3], adder_1_out[4], adder_1_out[5], adder_1_out[6], adder_1_out[7]);
  assign {controlled_buffer_1_out, controlled_buffer_1_out_2} = rom_4_data[3] ? xor_2_out : 8'bz;  // Controlled_Buffer controlled_buffer_11
  assign {controlled_buffer_1_out, controlled_buffer_1_out_2} = rom_4_data[2] ? not_3_out : 8'bz;  // Controlled_Buffer controlled_buffer_12
  assign {controlled_buffer_1_out, controlled_buffer_1_out_2} = rom_4_data[1] ? shifter_1_out : 8'bz;  // Controlled_Buffer controlled_buffer_13
  assign {controlled_buffer_1_out, controlled_buffer_1_out_2} = rom_4_data[0] ? shifter_2_out : 8'bz;  // Controlled_Buffer controlled_buffer_14
  Register #(.width(4)) register_6 (
    .D({nor_1_out, 1'b0}), .en(rom_5_data[7]), .clk(nand_5_out), .Q(register_6_q), .clr(or_3_out[6]));
  D_Flip_Flop d_ff_2 (
    .D(register_6_q[1]), .clk(rom_5_data[4]), .Q(d_ff_2_q[0]), .reset(or_3_out[6]));  // open: Qn, preset
  D_Flip_Flop d_ff_3 (
    .D(register_6_q[2]), .clk(rom_5_data[5]), .Q(d_ff_2_q[1]), .reset(or_3_out[6]));  // open: Qn, preset
  D_Flip_Flop d_ff_4 (
    .D(register_6_q[3]), .clk(rom_5_data[6]), .Q(d_ff_2_q[2]), .reset(or_3_out[6]));  // open: Qn, preset
  // also tied to GND on the sheet: {register_3_q[6], register_3_q[7]}

  // Notes on the sheet:
  //   Doesn't look good here but it works in real life
  //   Two's complement enable
  //   Programming-Mode-Toggle
  //   Address
  //   Value
  //   Value-Write
  //   Clock-Pulse
  //   Manual-Clock-Toggle
  //   contents of rom_1 (hex, n*v repeats v):
  //   fc 60 da f2 66 b6 be e0 fe f6 fc 60 da f2 66 b6 be e0 fe f6 fc 60 da f2 66 b6 be e0 fe f6 fc 60 da
  //   f2 66 b6 be e0 fe f6 fc 60 da f2 66 b6 be e0 fe f6 fc 60 da f2 66 b6 be e0 fe f6 fc 60 da f2 66 b6
  //   be e0 fe f6 fc 60 da f2 66 b6 be e0 fe f6 fc 60 da f2 66 b6 be e0 fe f6 fc 60 da f2 66 b6 be e0 fe
  //   f6 fc 60 da f2 66 b6 be e0 fe f6 fc 60 da f2 66 b6 be e0 fe f6 fc 60 da f2 66 b6 be e0 fe f6 fc 60
  //   da f2 66 b6 be e0 fe f6 fc 60 da f2 66 b6 be e0 fe f6 fc 60 da f2 66 b6 be e0 fe f6 fc 60 da f2 66
  //   b6 be e0 fe f6 fc 60 da f2 66 b6 be e0 fe f6 fc 60 da f2 66 b6 be e0 fe f6 fc 60 da f2 66 b6 be e0
  //   fe f6 fc 60 da f2 66 b6 be e0 fe f6 fc 60 da f2 66 b6 be e0 fe f6 fc 60 da f2 66 b6 be e0 fe f6 fc
  //   60 da f2 66 b6 be e0 fe f6 fc 60 da f2 66 b6 be e0 fe f6 fc 60 da f2 66 b6 10*fc 10*60 10*da 10*f2
  //   10*66 10*b6 10*be 10*e0 10*fe 10*f6 10*fc 10*60 10*da 10*f2 10*66 10*b6 10*be 10*e0 10*fe 10*f6
  //   10*fc 10*60 10*da 10*f2 10*66 6*b6 100*fc 100*60 56*da 256*0 fc 60 da f2 66 b6 be e0 fe f6 fc 60 da
  //   f2 66 b6 be e0 fe f6 fc 60 da f2 66 b6 be e0 fe f6 fc 60 da f2 66 b6 be e0 fe f6 fc 60 da f2 66 b6
  //   be e0 fe f6 fc 60 da f2 66 b6 be e0 fe f6 fc 60 da f2 66 b6 be e0 fe f6 fc 60 da f2 66 b6 be e0 fe
  //   f6 fc 60 da f2 66 b6 be e0 fe f6 fc 60 da f2 66 b6 be e0 fe f6 fc 60 da f2 66 b6 be e0 fe f6 fc 60
  //   da f2 66 b6 be e0 fe f6 fc 60 da f2 66 b6 be e0 fe e0 be b6 66 f2 da 60 fc f6 fe e0 be b6 66 f2 da
  //   60 fc f6 fe e0 be b6 66 f2 da 60 fc f6 fe e0 be b6 66 f2 da 60 fc f6 fe e0 be b6 66 f2 da 60 fc f6
  //   fe e0 be b6 66 f2 da 60 fc f6 fe e0 be b6 66 f2 da 60 fc f6 fe e0 be b6 66 f2 da 60 fc f6 fe e0 be
  //   b6 66 f2 da 60 fc f6 fe e0 be b6 66 f2 da 60 fc f6 fe e0 be b6 66 f2 da 60 fc f6 fe e0 be b6 66 f2
  //   da 60 fc f6 fe e0 be b6 66 f2 da 60 10*fc 10*60 10*da 10*f2 10*66 10*b6 10*be 10*e0 10*fe 10*f6
  //   10*fc 10*60 17*da 10*60 10*fc 10*f6 10*fe 10*e0 10*be 10*b6 10*66 10*f2 10*da 10*60 109*fc 57*60
  //   99*fc 128*0 128*2
  //   Microinstriction-Counter
  //   Inst-Reg
  //   Flg
  //   RAM
  //   ROM-Address
  //   OpCode
  //   contents of rom_2 (hex, n*v repeats v):
  //   10 80 6*0 10 0 21 5*0 10 0 21 5*0 10 20 6*0 10 20 6*0 10 0 22 5*0 10 0 22 5*0 10 0 20 5*0 10 0 20
  //   5*0 10 28 6*0 10 24 6*0 10 0 20 5*0 10 0 22 5*0 10 0 20 5*0 10 0 22 5*0 10 0 20 5*0 10 0 22 5*0 10 0
  //   20 5*0 10 0 20 5*0 10 0 22 5*0 10 20 6*0 10 0 22 5*0 10 8 0 20 4*0 10 8 0 20 4*0 10 0 20 5*0 10 0 20
  //   5*0 10 0 20 5*0 10 0 20 5*0 10 0 20 5*0 10 0 20 5*0 10 0 20 5*0 10 0 20 5*0 10 20 6*0 10 40 6*0 10
  //   20 6*0 10 20 6*0 10 0 21 5*0 10 20 6*0 10 20 206*0 10 80 6*0 10 0 21 5*0 10 0 21 5*0 10 20 6*0 10 20
  //   6*0 10 0 22 5*0 10 0 22 5*0 10 0 20 5*0 10 0 20 5*0 10 28 6*0 10 24 6*0 10 0 20 5*0 10 0 22 5*0 10 0
  //   20 5*0 10 0 22 5*0 10 0 20 5*0 10 0 22 5*0 10 0 20 5*0 10 0 20 5*0 10 0 22 5*0 10 20 6*0 10 0 22 5*0
  //   10 8 0 20 4*0 10 8 0 20 4*0 10 0 20 5*0 10 0 20 5*0 10 0 20 5*0 10 0 20 5*0 10 0 20 5*0 10 0 20 5*0
  //   10 0 20 5*0 10 0 20 5*0 10 20 6*0 10 40 6*0 10 20 6*0 10 20 6*0 10 0 21 5*0 10 20 6*0 10 20 206*0 10
  //   80 6*0 10 0 21 5*0 10 0 21 5*0 10 20 6*0 10 20 6*0 10 0 22 5*0 10 0 22 5*0 10 0 20 5*0 10 0 20 5*0
  //   10 28 6*0 10 24 6*0 10 0 20 5*0 10 0 22 5*0 10 0 20 5*0 10 0 22 5*0 10 0 20 5*0 10 0 22 5*0 10 0 20
  //   5*0 10 0 20 5*0 10 0 22 5*0 10 20 6*0 10 0 22 5*0 10 8 0 20 4*0 10 8 0 20 4*0 10 0 20 5*0 10 0 20
  //   5*0 10 0 20 5*0 10 0 20 5*0 10 0 20 5*0 10 0 20 5*0 10 0 20 5*0 10 0 20 5*0 10 20 6*0 10 40 6*0 10
  //   20 6*0 10 20 6*0 10 0 21 5*0 10 20 6*0 10 20 206*0 10 80 6*0 10 0 21 5*0 10 0 21 5*0 10 20 6*0 10 20
  //   6*0 10 0 22 5*0 10 0 22 5*0 10 0 20 5*0 10 0 20 5*0 10 28 6*0 10 24 6*0 10 0 20 5*0 10 0 22 5*0 10 0
  //   20 5*0 10 0 22 5*0 10 0 20 5*0 10 0 22 5*0 10 0 20 5*0 10 0 20 5*0 10 0 22 5*0 10 20 6*0 10 0 22 5*0
  //   10 8 0 20 4*0 10 8 0 20 4*0 10 0 20 5*0 10 0 20 5*0 10 0 20 5*0 10 0 20 5*0 10 0 20 5*0 10 0 20 5*0
  //   10 0 20 5*0 10 0 20 5*0 10 20 6*0 10 40 6*0 10 20 6*0 10 20 6*0 10 0 21 5*0 10 20 6*0 10 20 206*0 10
  //   80 6*0 10 0 21 5*0 10 0 21 5*0 10 20 6*0 10 20 6*0 10 0 22 5*0 10 0 22 5*0 10 0 20 5*0 10 0 20 5*0
  //   10 28 6*0 10 24 6*0 10 0 20 5*0 10 0 22 5*0 10 0 20 5*0 10 0 22 5*0 10 0 20 5*0 10 0 22 5*0 10 0 20
  //   5*0 10 0 20 5*0 10 0 22 5*0 10 20 6*0 10 0 22 5*0 10 8 0 20 4*0 10 8 0 20 4*0 10 0 20 5*0 10 0 20
  //   5*0 10 0 20 5*0 10 0 20 5*0 10 0 20 5*0 10 0 20 5*0 10 0 20 5*0 10 0 20 5*0 10 20 6*0 10 40 6*0 10
  //   20 6*0 10 20 6*0 10 0 21 5*0 10 20 6*0 10 20 206*0 10 80 6*0 10 0 21 5*0 10 0 21 5*0 10 20 6*0 10 20
  //   6*0 10 0 22 5*0 10 0 22 5*0 10 0 20 5*0 10 0 20 5*0 10 28 6*0 10 24 6*0 10 0 20 5*0 10 0 22 5*0 10 0
  //   20 5*0 10 0 22 5*0 10 0 20 5*0 10 0 22 5*0 10 0 20 5*0 10 0 20 5*0 10 0 22 5*0 10 20 6*0 10 0 22 5*0
  //   10 8 0 20 4*0 10 8 0 20 4*0 10 0 20 5*0 10 0 20 5*0 10 0 20 5*0 10 0 20 5*0 10 0 20 5*0 10 0 20 5*0
  //   10 0 20 5*0 10 0 20 5*0 10 20 6*0 10 40 6*0 10 20 6*0 10 20 6*0 10 0 21 5*0 10 20 6*0 10 20 206*0 10
  //   80 6*0 10 0 21 5*0 10 0 21 5*0 10 20 6*0 10 20 6*0 10 0 22 5*0 10 0 22 5*0 10 0 20 5*0 10 0 20 5*0
  //   10 28 6*0 10 24 6*0 10 0 20 5*0 10 0 22 5*0 10 0 20 5*0 10 0 22 5*0 10 0 20 5*0 10 0 22 5*0 10 0 20
  //   5*0 10 0 20 5*0 10 0 22 5*0 10 20 6*0 10 0 22 5*0 10 8 0 20 4*0 10 8 0 20 4*0 10 0 20 5*0 10 0 20
  //   5*0 10 0 20 5*0 10 0 20 5*0 10 0 20 5*0 10 0 20 5*0 10 0 20 5*0 10 0 20 5*0 10 20 6*0 10 40 6*0 10
  //   20 6*0 10 20 6*0 10 0 21 5*0 10 20 6*0 10 20 206*0 10 80 6*0 10 0 21 5*0 10 0 21 5*0 10 20 6*0 10 20
  //   6*0 10 0 22 5*0 10 0 22 5*0 10 0 20 5*0 10 0 20 5*0 10 28 6*0 10 24 6*0 10 0 20 5*0 10 0 22 5*0 10 0
  //   20 5*0 10 0 22 5*0 10 0 20 5*0 10 0 22 5*0 10 0 20 5*0 10 0 20 5*0 10 0 22 5*0 10 20 6*0 10 0 22 5*0
  //   10 8 0 20 4*0 10 8 0 20 4*0 10 0 20 5*0 10 0 20 5*0 10 0 20 5*0 10 0 20 5*0 10 0 20 5*0 10 0 20 5*0
  //   10 0 20 5*0 10 0 20 5*0 10 20 6*0 10 40 6*0 10 20 6*0 10 20 6*0 10 0 21 5*0 10 20 6*0 10 20
  //   contents of rom_3 (hex, n*v repeats v):
  //   50 7*0 50 d0 4 5*0 50 d0 1 5*0 50 54 6*0 50 51 6*0 50 d0 8 5*0 50 d0 2 5*0 50 9 4 5*0 50 6 1 5*0 50
  //   4 6*0 50 4 6*0 50 4 6*0 50 d0 6*0 50 4 6*0 50 d0 6*0 50 4 6*0 50 d0 6*0 50 4 6*0 50 4 6*0 50 d0 6*0
  //   50 4 6*0 50 d0 6*0 50 1 4 1 4*0 50 1 4 1 4*0 50 4 6*0 50 4 6*0 50 0 10 5*0 50 0 60 5*0 50 0 10 5*0
  //   50 0 60 5*0 50 0 10 5*0 50 0 60 5*0 50 60 6*0 50 7*0 50 10 6*0 50 50 6*0 50 d0 6*0 50 8 6*0 50 2
  //   206*0 50 7*0 50 d0 4 5*0 50 d0 1 5*0 50 54 6*0 50 51 6*0 50 d0 8 5*0 50 d0 2 5*0 50 9 4 5*0 50 6 1
  //   5*0 50 4 6*0 50 4 6*0 50 4 6*0 50 d0 6*0 50 4 6*0 50 d0 6*0 50 4 6*0 50 d0 6*0 50 4 6*0 50 4 6*0 50
  //   d0 6*0 50 4 6*0 50 d0 6*0 50 1 4 1 4*0 50 1 4 1 4*0 50 4 6*0 50 4 6*0 50 0 60 5*0 50 0 10 5*0 50 0
  //   10 5*0 50 0 60 5*0 50 0 10 5*0 50 0 60 5*0 50 60 6*0 50 7*0 50 10 6*0 50 50 6*0 50 d0 6*0 50 8 6*0
  //   50 2 206*0 50 7*0 50 d0 4 5*0 50 d0 1 5*0 50 54 6*0 50 51 6*0 50 d0 8 5*0 50 d0 2 5*0 50 9 4 5*0 50
  //   6 1 5*0 50 4 6*0 50 4 6*0 50 4 6*0 50 d0 6*0 50 4 6*0 50 d0 6*0 50 4 6*0 50 d0 6*0 50 4 6*0 50 4 6*0
  //   50 d0 6*0 50 4 6*0 50 d0 6*0 50 1 4 1 4*0 50 1 4 1 4*0 50 4 6*0 50 4 6*0 50 0 10 5*0 50 0 60 5*0 50
  //   0 60 5*0 50 0 10 5*0 50 0 10 5*0 50 0 60 5*0 50 60 6*0 50 7*0 50 10 6*0 50 50 6*0 50 d0 6*0 50 8 6*0
  //   50 2 206*0 50 7*0 50 d0 4 5*0 50 d0 1 5*0 50 54 6*0 50 51 6*0 50 d0 8 5*0 50 d0 2 5*0 50 9 4 5*0 50
  //   6 1 5*0 50 4 6*0 50 4 6*0 50 4 6*0 50 d0 6*0 50 4 6*0 50 d0 6*0 50 4 6*0 50 d0 6*0 50 4 6*0 50 4 6*0
  //   50 d0 6*0 50 4 6*0 50 d0 6*0 50 1 4 1 4*0 50 1 4 1 4*0 50 4 6*0 50 4 6*0 50 0 60 5*0 50 0 10 5*0 50
  //   0 60 5*0 50 0 10 5*0 50 0 10 5*0 50 0 60 5*0 50 60 6*0 50 7*0 50 10 6*0 50 50 6*0 50 d0 6*0 50 8 6*0
  //   50 2 206*0 50 7*0 50 d0 4 5*0 50 d0 1 5*0 50 54 6*0 50 51 6*0 50 d0 8 5*0 50 d0 2 5*0 50 9 4 5*0 50
  //   6 1 5*0 50 4 6*0 50 4 6*0 50 4 6*0 50 d0 6*0 50 4 6*0 50 d0 6*0 50 4 6*0 50 d0 6*0 50 4 6*0 50 4 6*0
  //   50 d0 6*0 50 4 6*0 50 d0 6*0 50 1 4 1 4*0 50 1 4 1 4*0 50 4 6*0 50 4 6*0 50 0 10 5*0 50 0 60 5*0 50
  //   0 10 5*0 50 0 60 5*0 50 0 60 5*0 50 0 10 5*0 50 60 6*0 50 7*0 50 10 6*0 50 50 6*0 50 d0 6*0 50 8 6*0
  //   50 2 206*0 50 7*0 50 d0 4 5*0 50 d0 1 5*0 50 54 6*0 50 51 6*0 50 d0 8 5*0 50 d0 2 5*0 50 9 4 5*0 50
  //   6 1 5*0 50 4 6*0 50 4 6*0 50 4 6*0 50 d0 6*0 50 4 6*0 50 d0 6*0 50 4 6*0 50 d0 6*0 50 4 6*0 50 4 6*0
  //   50 d0 6*0 50 4 6*0 50 d0 6*0 50 1 4 1 4*0 50 1 4 1 4*0 50 4 6*0 50 4 6*0 50 0 60 5*0 50 0 10 5*0 50
  //   0 10 5*0 50 0 60 5*0 50 0 60 5*0 50 0 10 5*0 50 60 6*0 50 7*0 50 10 6*0 50 50 6*0 50 d0 6*0 50 8 6*0
  //   50 2 206*0 50 7*0 50 d0 4 5*0 50 d0 1 5*0 50 54 6*0 50 51 6*0 50 d0 8 5*0 50 d0 2 5*0 50 9 4 5*0 50
  //   6 1 5*0 50 4 6*0 50 4 6*0 50 4 6*0 50 d0 6*0 50 4 6*0 50 d0 6*0 50 4 6*0 50 d0 6*0 50 4 6*0 50 4 6*0
  //   50 d0 6*0 50 4 6*0 50 d0 6*0 50 1 4 1 4*0 50 1 4 1 4*0 50 4 6*0 50 4 6*0 50 0 10 5*0 50 0 60 5*0 50
  //   0 60 5*0 50 0 10 5*0 50 0 60 5*0 50 0 10 5*0 50 60 6*0 50 7*0 50 10 6*0 50 50 6*0 50 d0 6*0 50 8 6*0
  //   50 2 206*0 50 7*0 50 d0 4 5*0 50 d0 1 5*0 50 54 6*0 50 51 6*0 50 d0 8 5*0 50 d0 2 5*0 50 9 4 5*0 50
  //   6 1 5*0 50 4 6*0 50 4 6*0 50 4 6*0 50 d0 6*0 50 4 6*0 50 d0 6*0 50 4 6*0 50 d0 6*0 50 4 6*0 50 4 6*0
  //   50 d0 6*0 50 4 6*0 50 d0 6*0 50 1 4 1 4*0 50 1 4 1 4*0 50 4 6*0 50 4 6*0 50 0 60 5*0 50 0 10 5*0 50
  //   0 60 5*0 50 0 10 5*0 50 0 60 5*0 50 0 10 5*0 50 60 6*0 50 7*0 50 10 6*0 50 50 6*0 50 d0 6*0 50 8 6*0
  //   50 2
  //   contents of rom_4 (hex, n*v repeats v):
  //   89*0 20 8*0 20 6*0 10 8*0 10 6*0 8 8*0 8 6*0 4 7*0 40 8*0 40 6*0 c0 8*0 c0 7*0 40 7*0 c0 6*0 2 7*0 1
  //   399*0 20 8*0 20 6*0 10 8*0 10 6*0 8 8*0 8 6*0 4 7*0 40 8*0 40 6*0 c0 8*0 c0 7*0 40 7*0 c0 6*0 2 7*0
  //   1 399*0 20 8*0 20 6*0 10 8*0 10 6*0 8 8*0 8 6*0 4 7*0 40 8*0 40 6*0 c0 8*0 c0 7*0 40 7*0 c0 6*0 2
  //   7*0 1 399*0 20 8*0 20 6*0 10 8*0 10 6*0 8 8*0 8 6*0 4 7*0 40 8*0 40 6*0 c0 8*0 c0 7*0 40 7*0 c0 6*0
  //   2 7*0 1 399*0 20 8*0 20 6*0 10 8*0 10 6*0 8 8*0 8 6*0 4 7*0 40 8*0 40 6*0 c0 8*0 c0 7*0 40 7*0 c0
  //   6*0 2 7*0 1 399*0 20 8*0 20 6*0 10 8*0 10 6*0 8 8*0 8 6*0 4 7*0 40 8*0 40 6*0 c0 8*0 c0 7*0 40 7*0
  //   c0 6*0 2 7*0 1 399*0 20 8*0 20 6*0 10 8*0 10 6*0 8 8*0 8 6*0 4 7*0 40 8*0 40 6*0 c0 8*0 c0 7*0 40
  //   7*0 c0 6*0 2 7*0 1 399*0 20 8*0 20 6*0 10 8*0 10 6*0 8 8*0 8 6*0 4 7*0 40 8*0 40 6*0 c0 8*0 c0 7*0
  //   40 7*0 c0 6*0 2 7*0 1
  //   contents of rom_5 (hex, n*v repeats v):
  //   90*0 80 7*0 80 7*0 80 7*0 80 7*0 80 7*0 80 7*0 80 7*0 80 7*0 80 6*0 80 8*0 80 8*0 80 7*0 80 6*0 80
  //   7*0 80 6*0 10 7*0 10 7*0 20 7*0 20 7*0 40 7*0 40 31*0 8 8*0 8 6*0 8 7*0 8 296*0 80 7*0 80 7*0 80 7*0
  //   80 7*0 80 7*0 80 7*0 80 7*0 80 7*0 80 6*0 80 8*0 80 8*0 80 7*0 80 6*0 80 7*0 80 6*0 10 7*0 10 7*0 20
  //   7*0 20 7*0 40 7*0 40 31*0 8 8*0 8 6*0 8 7*0 8 296*0 80 7*0 80 7*0 80 7*0 80 7*0 80 7*0 80 7*0 80 7*0
  //   80 7*0 80 6*0 80 8*0 80 8*0 80 7*0 80 6*0 80 7*0 80 6*0 10 7*0 10 7*0 20 7*0 20 7*0 40 7*0 40 31*0 8
  //   8*0 8 6*0 8 7*0 8 296*0 80 7*0 80 7*0 80 7*0 80 7*0 80 7*0 80 7*0 80 7*0 80 7*0 80 6*0 80 8*0 80 8*0
  //   80 7*0 80 6*0 80 7*0 80 6*0 10 7*0 10 7*0 20 7*0 20 7*0 40 7*0 40 31*0 8 8*0 8 6*0 8 7*0 8 296*0 80
  //   7*0 80 7*0 80 7*0 80 7*0 80 7*0 80 7*0 80 7*0 80 7*0 80 6*0 80 8*0 80 8*0 80 7*0 80 6*0 80 7*0 80
  //   6*0 10 7*0 10 7*0 20 7*0 20 7*0 40 7*0 40 31*0 8 8*0 8 6*0 8 7*0 8 296*0 80 7*0 80 7*0 80 7*0 80 7*0
  //   80 7*0 80 7*0 80 7*0 80 7*0 80 6*0 80 8*0 80 8*0 80 7*0 80 6*0 80 7*0 80 6*0 10 7*0 10 7*0 20 7*0 20
  //   7*0 40 7*0 40 31*0 8 8*0 8 6*0 8 7*0 8 296*0 80 7*0 80 7*0 80 7*0 80 7*0 80 7*0 80 7*0 80 7*0 80 7*0
  //   80 6*0 80 8*0 80 8*0 80 7*0 80 6*0 80 7*0 80 6*0 10 7*0 10 7*0 20 7*0 20 7*0 40 7*0 40 31*0 8 8*0 8
  //   6*0 8 7*0 8 296*0 80 7*0 80 7*0 80 7*0 80 7*0 80 7*0 80 7*0 80 7*0 80 7*0 80 6*0 80 8*0 80 8*0 80
  //   7*0 80 6*0 80 7*0 80 6*0 10 7*0 10 7*0 20 7*0 20 7*0 40 7*0 40 31*0 8 8*0 8 6*0 8 7*0 8
  //   Clock-Module
  //   Ctr
  //   Control-Logic
  //   Output
  //   Op-Code
  //   Reset
  //   Bus
  //   Bus
  //   Command-Pins
  //   Program-Counter
  //   A-Register
  //   B-Register
  //   Program
  //   contents of rom_6 (hex, n*v repeats v):
  //   23 14 24 1 0 9 7 9 12 1c 8 20 3 14 1a 0 20 8
  //   ALU
  //   HLT, RST, CRST, II, FST, LST, RW, RO --- RI, CO, JMP, CNT, AO, AI, BO, BI --- SUB, ADD, AND, OR, XOR, NOT, SHR, SHL --- FLGW, CMP, CARY, ZERO, OUT, #, #, #
  //   Up to 256 lines of code*
  //   Flag-Register
endmodule
